// Logisim project nand2tetris.circ as structural Verilog
module my_or (
  input  ain,
  input  bin,
  output myout
);

  wire nand_1_out, nand_2_out;

  nand nand_1 (nand_1_out, ain, ain);
  nand nand_2 (nand_2_out, bin, bin);
  nand nand_3 (myout, nand_1_out, nand_2_out);
endmodule

module my_not (
  input  myin,
  output myout
);

  nand nand_1 (myout, myin, myin);
endmodule

module my_and (
  input  a,
  input  b,
  output MyOut
);

  wire nand_1_out, nand_2_out;

  nand nand_1 (nand_1_out, a, b);
  nand nand_2 (nand_2_out, a, b);
  nand nand_3 (MyOut, nand_1_out, nand_2_out);
endmodule

module my_XOR (
  input  a,
  input  b,
  output MyOut
);

  wire and_1_out, and_2_out, not_1_out, not_2_out;

  not not_1 (not_1_out, a);
  not not_2 (not_2_out, b);
  and and_1 (and_1_out, not_1_out, b);
  and and_2 (and_2_out, a, not_2_out);
  or or_1 (MyOut, and_1_out, and_2_out);
endmodule

module Mux (
  input  a,
  input  b,
  input  sel,
  output MyOut
);

  wire and_1_out, and_2_out, and_3_out, not_1_out, or_1_out;

  and and_1 (and_1_out, a, b);
  and and_2 (and_2_out, b, sel);
  and and_3 (and_3_out, a, not_1_out);
  not not_1 (not_1_out, sel);
  or or_1 (or_1_out, and_1_out, and_2_out);
  or or_2 (MyOut, or_1_out, and_3_out);
endmodule

module DMux (
  input  MyIn,
  input  sel,
  output a,
  output b
);

  wire not_1_out;

  not not_1 (not_1_out, sel);
  and and_1 (a, MyIn, not_1_out);
  and and_2 (b, MyIn, sel);
endmodule

module Not16 (
  input  [15:0] MyIn,
  output [15:0] MyOut
);

  assign MyOut = ~MyIn;  // NOT_Gate not_1, 16 bits wide
endmodule

module my_HA (
  input  a,
  input  b,
  output sum,
  output carry
);

  xor xor_1 (sum, a, b);
  and and_1 (carry, a, b);
endmodule

module my_FA (
  input  a,
  input  b,
  input  c,
  output sum,
  output carry
);

  wire and_1_out, and_2_out, and_3_out, and_4_out, xor_1_out;

  ExactlyOne xor_1 (.out(xor_1_out), .in0(a), .in1(b), .in2(c));
  and and_1 (and_1_out, a, b, c);
  and and_2 (and_2_out, b, c);
  and and_3 (and_3_out, c, a);
  and and_4 (and_4_out, a, b);
  or or_1 (carry, and_2_out, and_3_out, and_4_out);
  or or_2 (sum, xor_1_out, and_1_out);
endmodule

module my_FA2 (
  input  a,
  input  b,
  input  c,
  output sum,
  output carry
);

  wire my_ha_1_carry, my_ha_1_sum, my_ha_2_carry;

  my_HA my_ha_1 (.a(a), .b(b), .sum(my_ha_1_sum), .carry(my_ha_1_carry));
  my_HA my_ha_2 (.a(my_ha_1_sum), .b(c), .sum(sum), .carry(my_ha_2_carry));
  or or_1 (carry, my_ha_2_carry, my_ha_1_carry);
endmodule

module my_Add16 (
  input  [15:0] a,
  input  [15:0] b,
  output [15:0] sum
);

  wire adder_1_cout, adder_2_cout, adder_3_cout, adder_4_cout, adder_5_cout, adder_6_cout, adder_7_cout,
       adder_8_cout, adder_9_cout, adder_10_cout, adder_11_cout, adder_12_cout, adder_13_cout, adder_14_cout,
       adder_15_cout;

  Adder #(.width(1)) adder_1 (.a(a[0]), .b(b[0]), .out(sum[0]), .cout(adder_1_cout));  // open: cin
  Adder #(.width(1)) adder_2 (.a(a[1]), .b(b[1]), .out(sum[1]), .cin(adder_1_cout), .cout(adder_2_cout));
  Adder #(.width(1)) adder_3 (.a(a[2]), .b(b[2]), .out(sum[2]), .cin(adder_2_cout), .cout(adder_3_cout));
  Adder #(.width(1)) adder_4 (.a(a[3]), .b(b[3]), .out(sum[3]), .cin(adder_3_cout), .cout(adder_4_cout));
  Adder #(.width(1)) adder_5 (.a(a[4]), .b(b[4]), .out(sum[4]), .cin(adder_4_cout), .cout(adder_5_cout));
  Adder #(.width(1)) adder_6 (.a(a[5]), .b(b[5]), .out(sum[5]), .cin(adder_5_cout), .cout(adder_6_cout));
  Adder #(.width(1)) adder_7 (.a(a[6]), .b(b[6]), .out(sum[6]), .cin(adder_6_cout), .cout(adder_7_cout));
  Adder #(.width(1)) adder_8 (.a(a[7]), .b(b[7]), .out(sum[7]), .cin(adder_7_cout), .cout(adder_8_cout));
  Adder #(.width(1)) adder_9 (.a(a[8]), .b(b[8]), .out(sum[8]), .cin(adder_8_cout), .cout(adder_9_cout));
  Adder #(.width(1)) adder_10 (.a(a[9]), .b(b[9]), .out(sum[9]), .cin(adder_9_cout), .cout(adder_10_cout));
  Adder #(.width(1)) adder_11 (.a(a[10]), .b(b[10]), .out(sum[10]), .cin(adder_10_cout), .cout(adder_11_cout));
  Adder #(.width(1)) adder_12 (.a(a[11]), .b(b[11]), .out(sum[11]), .cin(adder_11_cout), .cout(adder_12_cout));
  Adder #(.width(1)) adder_13 (.a(a[12]), .b(b[12]), .out(sum[12]), .cin(adder_12_cout), .cout(adder_13_cout));
  Adder #(.width(1)) adder_14 (.a(a[13]), .b(b[13]), .out(sum[13]), .cin(adder_13_cout), .cout(adder_14_cout));
  Adder #(.width(1)) adder_15 (.a(a[14]), .b(b[14]), .out(sum[14]), .cin(adder_14_cout), .cout(adder_15_cout));
  Adder #(.width(1)) adder_16 (.a(a[15]), .b(b[15]), .out(sum[15]), .cin(adder_15_cout));  // open: cout
endmodule

module my_CLA4 (
  input  [3:0] a,
  input  [3:0] b,
  output [3:0] sum
);

  wire and_1_out, and_2_out, and_3_out, and_4_out, or_1_out, or_2_out, or_3_out;

  and and_1 (and_1_out, a[0], b[0]);
  and and_2 (and_2_out, a[1], b[1]);
  and and_3 (and_3_out, a[2], b[2]);
  and and_4 (and_4_out, a[3], b[3]);
  or or_1 (or_1_out, and_1_out, and_2_out);
  or or_2 (or_2_out, or_1_out, and_3_out);
  or or_3 (or_3_out, or_2_out, and_4_out);
  Adder #(.width(1)) adder_1 (.a(a[0]), .b(b[0]), .out(sum[0]));  // open: cin, cout
  Adder #(.width(1)) adder_2 (.a(a[1]), .b(b[1]), .out(sum[1]), .cin(or_1_out));  // open: cout
  Adder #(.width(1)) adder_3 (.a(a[2]), .b(b[2]), .out(sum[2]), .cin(or_2_out));  // open: cout
  Adder #(.width(1)) adder_4 (.a(a[3]), .b(b[3]), .out(sum[3]), .cin(or_3_out));  // open: cout
endmodule
